# Fritzing sketch ParkDistance (saved by Fritzing 0.9.3b)
circuit board: 11.4653cm x 5.60916cm
breadboards: 1

parts:
  J1 = female pin header, 8 pins [form="♀ (female)"]
  J2 = female pin header, 8 pins [form="♀ (female)"]
  J3 = female pin header, 8 pins [form="♀ (female)"]  # not connected
  J4 = female pin header, 8 pins [form="♀ (female)"]  # not connected
  J5 = female pin header, 8 pins [form="♀ (female)"]  # not connected
  J6 = female pin header, 8 pins [form="♀ (female)"]  # not connected
  MAX7219 = STP16CP05 [package=so-24dw]
  10k = Resistor [tolerance=±5% resistance=10k package="0805 [SMD]"]
  X1 = USB Connectors [package=usb-minib-nostop]
  C1 = Tantalum Capacitor [capacitance=1µF package="B 3528 [SMD, tantalum]"]

nets:
  N1: J1.pin1, MAX7219.SDO
  N2: J1.pin2, MAX7219.OUT9
  N3: J1.pin3, MAX7219.OUT0
  N4: J1.pin4, MAX7219.OUT12
  N5: J1.pin5, MAX7219.CLK
  N6: J1.pin6, MAX7219.OUT11
  N7: J1.pin7, MAX7219.REXT
  N8: J1.pin8, MAX7219.OUT3
  N9: J2.pin1, MAX7219.OUT2
  N10: J2.pin2, MAX7219.OUT6
  N11: J2.pin3, MAX7219.OUT10
  N12: J2.pin4, MAX7219.~OE
  N13: J2.pin5, MAX7219.SDI
  N14: J2.pin6, MAX7219.OUT15
  N15: J2.pin7, MAX7219.OUT1
  N16: J2.pin8, MAX7219.OUT5
  N17: MAX7219.LE, MAX7219.OUT4, X1.GND, C1.-
  N18: MAX7219.OUT13, 10k.Pin_0
  N19: MAX7219.OUT14, 10k.Pin_1, X1.VBUS, C1.+
